# Fritzing sketch buzzer_led_song (saved by Fritzing 0.9.3b)
circuit board: 8.46667cm x 5.64444cm
breadboards: 1

parts:
  J1 = Piezo Speaker
  Part1 = Arduino Uno (Rev3)
  LED1 = LED - 5mm [color="Red (633nm)" package="5 mm [THT]"]
  LED2 = LED - 5mm [color="Red (633nm)" package="5 mm [THT]"]
  LED3 = LED - 5mm [color="Red (633nm)" package="5 mm [THT]"]
  LED4 = LED - 5mm [color="Red (633nm)" package="5 mm [THT]"]
  LED5 = LED - 5mm [color="Red (633nm)" package="5 mm [THT]"]
  LED6 = LED - 5mm [color="Red (633nm)" package="5 mm [THT]"]
  LED7 = LED - 5mm [color="Red (633nm)" package="5 mm [THT]"]
  R1 = Resistor [tolerance=±5% resistance=220 package=THT]
  R2 = Resistor [tolerance=±5% resistance=220 package=THT]
  R3 = Resistor [tolerance=±5% resistance=220 package=THT]
  R4 = Resistor [tolerance=±5% resistance=220 package=THT]
  R5 = Resistor [tolerance=±5% resistance=220 package=THT]
  R6 = Resistor [tolerance=±5% resistance=220 package=THT]
  R7 = Resistor [tolerance=±5% resistance=220 package=THT]

nets:
  N1: J1.pin1, Part1.GND
  N2: J1.pin2, Part1.D13/SCK
  N3: Part1.D8, R5.Pin_0
  N4: Part1.D9_PWM, R2.Pin_0
  N5: Part1.D10_PWM/SS, R1.Pin_0
  N6: Part1.D11_PWM/MOSI, R3.Pin_0
  N7: Part1.D2, R4.Pin_0
  N8: Part1.D4, R6.Pin_0
  N9: Part1.D7, R7.Pin_0
  N10: LED1.anode, R1.Pin_1
  N11: LED2.anode, R2.Pin_1
  N12: LED3.anode, R5.Pin_1
  N13: LED4.anode, R7.Pin_1
  N14: LED5.anode, R6.Pin_1
  N15: LED6.anode, R4.Pin_1
  N16: LED7.anode, R3.Pin_1

// code stored in the sketch: buzzer_led_song.ino
/*
  Light LEDs to the tune produced by a buzzer
*/


#include "pitches.h" //include this library

const int BUZZER_PIN = 2; // Arduino pin connected to Buzzer's pin

// notes in the melody:
int melody[] = {
NOTE_C4, NOTE_G3,NOTE_G3, NOTE_GS3, NOTE_G3,0, NOTE_B3, NOTE_C4};

// note durations: 4 = quarter note, 8 = eighth note, etc.:
int noteDurations[] = {
   4, 8, 8, 4,4,4,4,4 
};

//LED pins
int leds[] = {
   3,5 , 6,7, 8, 9,12,13,
};

void setup() {
  // set all pins to output mode
  pinMode(BUZZER_PIN, OUTPUT);       
  pinMode(3, OUTPUT);       
  pinMode(5, OUTPUT);       
  pinMode(6, OUTPUT);     
  pinMode(7, OUTPUT);       
  pinMode(8, OUTPUT);       
  pinMode(9, OUTPUT);      
  pinMode(12, OUTPUT);     
  pinMode(13, OUTPUT);     
}

void loop() {
     // iterate over the notes of the melody:
   for (int thisNote = 0; thisNote < 8; thisNote++) {
    //iterate over the leds
    for(int thisLed = 0; thisLed < 8; thisLed++){
        // to calculate the note duration, take one second
      // divided by the note type.
      //e.g. quarter note = 1000 / 4, eighth note = 1000/8, etc.
      int noteDuration = 1000/noteDurations[thisNote];
      //turn the current led on
      digitalWrite(leds[thisLed], HIGH);
      tone(BUZZER_PIN, melody[thisNote],noteDuration);
      //pause for the note's duration plus 30 ms:
      delay(noteDuration +30);
      //turn the current led off
      digitalWrite(leds[thisLed], LOW);
      }
   }
}
