# Fritzing sketch LCD_photoresistor (saved by Fritzing 0.9.3b)
circuit board: 6.88566cm x 5.36311cm
breadboards: 2

parts:
  LCD1 = LCD screen
  R2 = Resistor [tolerance=±5% resistance=220 package=THT]
  Arduino1 = Arduino Uno (Rev3)
  R3 = Photocell (LDR) [package=THT]
  R4 = Resistor [tolerance=±5% resistance=220 package=THT]

nets:
  VSS: LCD1.VSS, LCD1.R/W, LCD1.LED-, Arduino1.GND, R4.Pin_1
  VDD: LCD1.VDD, R2.Pin_1, Arduino1.5V, R3.pin_0
  N1: LCD1.V0, R3.pin_1, R4.Pin_0
  N2: LCD1.RS, Arduino1.D12/MISO
  N3: LCD1.E, Arduino1.D11_PWM/MOSI
  N4: LCD1.DB4, Arduino1.D5_PWM
  N5: LCD1.DB5, Arduino1.D4
  N6: LCD1.DB6, Arduino1.D3_PWM
  N7: LCD1.DB7, Arduino1.D2
  N8: LCD1.LED+, R2.Pin_0

notes:
  Code and more on character LCDs at http://arduino.cc/en/Tutorial/LiquidCrystal

// code stored in the sketch: ldr.ino
/* 
 * LDR Light Level Display on 16X2 LCD
 */
 
#include <LiquidCrystal.h>
LiquidCrystal lcd(12, 11, 5, 4, 3, 2);

void setup() { //initialise for at least 2s
  lcd.begin(16, 2);
  lcd.print("INITIALISING");
  delay(500);
  lcd.print(".");
  delay(500);
  lcd.print(".");  
  delay(500);
  lcd.print(".");
  delay(500);
  lcd.print(".");  
  delay(500);
}
void loop()
{
 int sensorValue = analogRead(A0);
 double dV = sensorValue;
 double le = (dV/1023)*100;  //display in percentage
 int level = le;
 lcd.clear();
 lcd.setCursor(0, 0);
 lcd.print("LIGHT LEVEL:");
 lcd.print(level);
 lcd.print("%");
 lcd.setCursor(0, 1);
 
 if ((level >= 0) && (level <= 5))
 {
  lcd.print("VERY DARK"); 
 }
 else if ((level > 5) && (level <= 10))
 {
  lcd.print("DARK"); 
 }
 else if ((level > 10) && (level <= 50))
 {
  lcd.print("BRIGHT"); 
 }
 else 
 {
  lcd.print("VERY BRIGHT"); 
 }
 
 delay(500); 
}
