# Fritzing sketch twobuttons (saved by Fritzing 0.9.3b)
breadboards: 1

parts:
  S1 = Momentary Switch [package=ksa_sealed_tac_switch]
  S2 = Momentary Switch [package=ksa_sealed_tac_switch]
  LED1 = LED - 5mm [color="Red (633nm)" package="5 mm [THT]"]
  R1 = Resistor [tolerance=±5% resistance=220 package="0402 [SMD]"]
  R2 = Resistor [tolerance=±5% resistance=220 package="0402 [SMD]"]
  R3 = Resistor [tolerance=±5% resistance=220 package="0402 [SMD]"]
  Part1 = Arduino Uno (Rev3)

nets:
  N1: S1.1, S2.3, Part1.5V
  N2: S1.3, Part1.D8
  N3: S2.1, R2.Pin_0, Part1.D2
  N4: LED1.cathode, R2.Pin_1, R3.Pin_0, Part1.GND
  N5: LED1.anode, R1.Pin_0
  N6: R1.Pin_1, Part1.D4

// code stored in the sketch: 2buttons.ino
/*
  Using 2 buttons to turn 1 LED on and off
*/

const int button = 4;            // pin 4 for the first button
const int button2 = 2;            // pin 2 for the second button
const int led = 8;                // pin 8 for the LED
int ledflag=0;                   // LED status flag

void setup() {
  pinMode(button,INPUT);         // define first button as an input
  pinMode(button2,INPUT);         // define second button as an input  
  pinMode(led,OUTPUT);           // define LED as an output
  digitalWrite(led,LOW);         // turn output off just in case
}

void loop() {
  if (digitalRead(button)==HIGH || digitalRead(button2)==HIGH){ // if button is pressed
    if (ledflag==0) {             // and the status flag is LOW
      ledflag=1;                  // make status flag HIGH
      digitalWrite(led,HIGH);     // and turn on the LED
      }                           // 
    else {                        // otherwise...
      ledflag=0;                  // make status flag LOW
      digitalWrite(led,LOW);      // and turn off the LED
    }
  delay(1000);                    // wait a sec for the 
  }                               // hardware to stabilize
}                                 // begin again
